// Logisim project aiALU.circ as structural Verilog
module aiALU (
  input  [7:0] in_1,
  input  [7:0] in_2,
  input  in_3,
  input  in_4,
  output [7:0] out_5,
  output [7:0] out_6
);

  // Probe on in_1
  // Probe on out_5
  aiArith aiarith_1 (.A(in_1), .B(in_2), .in_3(in_3), .in_4(in_4), .out_5(out_5), .out_6(out_6));
  // Probe on in_2
  // Probe on out_6
endmodule

module aiArith (
  input  [7:0] A,
  input  [7:0] B,
  input  in_3,
  input  in_4,
  output [7:0] out_5,
  output [7:0] out_6
);

  // Probe on out_5
  _8bit_Adder u_8bit_adder_1 (
    .in_15(B[0]), .in_16(A[0]), .in_14(B[1]), .in_13(A[1]), .in_12(B[2]), .in_11(A[2]), .in_10(B[3]),
    .in_9(A[3]), .in_8(B[4]), .in_7(A[4]), .in_6(B[5]), .in_5(A[5]), .in_4(B[6]), .in_3(A[6]), .in_2(B[7]),
    .in_1(A[7]), .out_20(out_5[7]), .out_21(out_5[6]), .out_22(out_5[5]), .out_23(out_5[4]),
    .out_24(out_5[3]), .out_25(out_5[2]), .out_26(out_5[1]), .out_27(out_5[0]), .in_17(in_4), .in_18(in_3));  // open: out_19
  _8bit_Subtractor u_8bit_subtractor_1 (.in_1(A), .in_2(B), .out_5(out_6), .in_3(in_3), .in_4(in_4));
  // Probe on out_6
endmodule

module HalfAdder (
  input  A,
  input  B,
  output S,
  output C
);

  xor xor_1 (S, A, B);
  and and_1 (C, A, B);
endmodule

module FullAdder (
  input  A,
  input  B,
  input  Cin,
  output Cout,
  output S
);

  wire halfadder_1_c, halfadder_2_c, halfadder_2_s;

  or or_1 (Cout, halfadder_2_c, halfadder_1_c);
  HalfAdder halfadder_1 (.A(halfadder_2_s), .B(Cin), .S(S), .C(halfadder_1_c));
  HalfAdder halfadder_2 (.A(A), .B(B), .S(halfadder_2_s), .C(halfadder_2_c));
endmodule

module _8bit_Adder (
  input  in_1,
  input  in_2,
  input  in_3,
  input  in_4,
  input  in_5,
  input  in_6,
  input  in_7,
  input  in_8,
  input  in_9,
  input  in_10,
  input  in_11,
  input  in_12,
  input  in_13,
  input  in_14,
  input  in_15,
  input  in_16,
  input  in_17,
  input  in_18,
  output out_19,
  output out_20,
  output out_21,
  output out_22,
  output out_23,
  output out_24,
  output out_25,
  output out_26,
  output out_27
);

  wire fulladder_2_cout, fulladder_3_cout, fulladder_4_cout, fulladder_5_cout, fulladder_6_cout,
       fulladder_7_cout, fulladder_8_cout, fulladder_9_cout, fulladder_9_s, or_1_out;

  FullAdder fulladder_1 (.A(in_2), .B(in_1), .Cin(fulladder_2_cout), .S(out_20), .Cout(out_19));
  FullAdder fulladder_2 (.A(in_4), .B(in_3), .Cin(fulladder_3_cout), .S(out_21), .Cout(fulladder_2_cout));
  FullAdder fulladder_3 (.A(in_6), .B(in_5), .Cin(fulladder_4_cout), .S(out_22), .Cout(fulladder_3_cout));
  FullAdder fulladder_4 (.A(in_8), .B(in_7), .Cin(fulladder_5_cout), .S(out_23), .Cout(fulladder_4_cout));
  FullAdder fulladder_5 (.A(in_10), .B(in_9), .Cin(fulladder_6_cout), .S(out_24), .Cout(fulladder_5_cout));
  FullAdder fulladder_6 (.A(in_12), .B(in_11), .Cin(fulladder_7_cout), .S(out_25), .Cout(fulladder_6_cout));
  FullAdder fulladder_7 (.A(in_14), .B(in_13), .Cin(fulladder_8_cout), .S(out_26), .Cout(fulladder_7_cout));
  FullAdder fulladder_8 (.A(in_16), .B(in_15), .Cin(or_1_out), .S(out_27), .Cout(fulladder_8_cout));
  FullAdder fulladder_9 (.A(in_18), .B(in_17), .Cin(in_18), .S(fulladder_9_s), .Cout(fulladder_9_cout));
  or or_1 (or_1_out, fulladder_9_cout, fulladder_9_s);
endmodule

module _8bit_Subtractor (
  input  [7:0] in_1,
  input  [7:0] in_2,
  input  in_3,
  input  in_4,
  output [7:0] out_5
);

  wire [7:0] not_1_out;

  assign not_1_out = ~in_2;  // NOT_Gate not_1, 8 bits wide
  _8bit_Adder u_8bit_adder_1 (
    .in_15(not_1_out[0]), .in_16(in_1[0]), .in_14(not_1_out[1]), .in_13(in_1[1]), .in_12(not_1_out[2]),
    .in_11(in_1[2]), .in_10(not_1_out[3]), .in_9(in_1[3]), .in_8(not_1_out[4]), .in_7(in_1[4]),
    .in_6(not_1_out[5]), .in_5(in_1[5]), .in_4(not_1_out[6]), .in_3(in_1[6]), .in_2(not_1_out[7]),
    .in_1(in_1[7]), .out_20(out_5[7]), .out_21(out_5[6]), .out_22(out_5[5]), .out_23(out_5[4]),
    .out_24(out_5[3]), .out_25(out_5[2]), .out_26(out_5[1]), .out_27(out_5[0]), .in_17(in_4), .in_18(in_3));  // open: out_19
endmodule
